# Fritzing sketch bme280_bb (saved by Fritzing 0.9.3b)
stripboards: 1

parts:
  J1 = shrouded pin header, 28 pins [form="♂ (shrouded male)"]
  LED2 = LED - 3mm [color="Red (633nm)" package="3 mm [THT]"]
  S1 = Pushbutton [package="[SMD]"]
  J2 = double row male pin header, 4 pins [form="♂ (male)"]
  J3 = double row male pin header, 4 pins [form="♂ (male)"]
  R1 = Resistor [tolerance=±5% resistance=330 package=THT]

nets:
  N1: J1.pin1, J2.pin1, J3.pin4
  N2: J1.pin2, J2.pin3, J3.pin2
  N3: J1.pin3, J2.pin4, J3.pin1
  N4: J1.pin18, S1.Pin_3, S1.Pin_4, J3.pin3, R1.Pin_1
  N5: J1.pin19, LED2.anode
  N6: J1.pin23, S1.Pin_1, S1.Pin_2
  N7: J1.pin26, J2.pin2
  N8: LED2.cathode, R1.Pin_0
